// Logisim project snakeOK.circ as structural Verilog: 32 circuits, main circuit main
module main (
  input  reset
);

  wire bas_out, clock_1_out, droite_out, gauche_out, general_mothafucka_1_reset_2, haut_out, not_1_out,
       or_1_out;
  wire [6:0] general_mothafucka_1_out_16;
  wire [7:0] general_mothafucka_1_out_7, general_mothafucka_1_out_8, general_mothafucka_1_out_9,
       general_mothafucka_1_out_10, general_mothafucka_1_out_11, general_mothafucka_1_out_12,
       general_mothafucka_1_out_13, general_mothafucka_1_out_14;

  Button haut (.out(haut_out));
  Button gauche (.out(gauche_out));
  Button bas (.out(bas_out));
  not not_1 (not_1_out, reset);
  Clock clock_1 (.out(clock_1_out));
  LED L10 (.in(general_mothafucka_1_out_16[6]));
  LED L9 ();  // open: in
  LED L21 ();  // open: in
  LED L20 (.in(general_mothafucka_1_out_16[5]));
  LED L32 (.in(general_mothafucka_1_out_16[4]));
  LED L31 ();  // open: in
  LED L43 (.in(general_mothafucka_1_out_16[3]));
  LED L44 ();  // open: in
  LED L55 (.in(general_mothafucka_1_out_16[2]));
  LED L54 ();  // open: in
  Button droite (.out(droite_out));
  LED L11 ();  // open: in
  LED L22 (.in(general_mothafucka_1_out_16[0]));
  LED L33 ();  // open: in
  LED L45 (.in(general_mothafucka_1_out_16[1]));
  LED L56 ();  // open: in
  or or_1 (or_1_out, not_1_out, general_mothafucka_1_reset_2);
  general_mothafucka general_mothafucka_1 (
    .g(gauche_out), .d(droite_out), .h(haut_out), .b(bas_out), .reset(or_1_out), .clock(clock_1_out),
    .out_7(general_mothafucka_1_out_7), .out_8(general_mothafucka_1_out_8),
    .out_9(general_mothafucka_1_out_9), .out_10(general_mothafucka_1_out_10),
    .out_11(general_mothafucka_1_out_11), .out_12(general_mothafucka_1_out_12),
    .out_13(general_mothafucka_1_out_13), .out_14(general_mothafucka_1_out_14),
    .reset_2(general_mothafucka_1_reset_2), .out_16(general_mothafucka_1_out_16));
  DotMatrix #(.inputtype("row"), .matrixcols(8), .matrixrows(8)) dotmatrix_1 (
    .row0(general_mothafucka_1_out_7), .row1(general_mothafucka_1_out_8), .row2(general_mothafucka_1_out_9),
    .row3(general_mothafucka_1_out_10), .row4(general_mothafucka_1_out_11),
    .row5(general_mothafucka_1_out_12), .row6(general_mothafucka_1_out_13), .row7(general_mothafucka_1_out_14));
  LED L3 (.in(general_mothafucka_1_out_7[5]));
  LED L1 (.in(general_mothafucka_1_out_7[7]));
  LED L2 (.in(general_mothafucka_1_out_7[6]));
  LED L13 (.in(general_mothafucka_1_out_8[6]));
  LED L12 (.in(general_mothafucka_1_out_8[7]));
  LED L14 (.in(general_mothafucka_1_out_8[5]));
  LED L24 (.in(general_mothafucka_1_out_9[6]));
  LED L23 (.in(general_mothafucka_1_out_9[7]));
  LED L25 (.in(general_mothafucka_1_out_9[5]));
  LED L34 (.in(general_mothafucka_1_out_10[7]));
  LED L35 (.in(general_mothafucka_1_out_10[6]));
  LED L36 (.in(general_mothafucka_1_out_10[5]));
  LED L48 (.in(general_mothafucka_1_out_11[5]));
  LED L46 (.in(general_mothafucka_1_out_11[7]));
  LED L47 (.in(general_mothafucka_1_out_11[6]));
  LED L57 (.in(general_mothafucka_1_out_12[7]));
  LED L58 (.in(general_mothafucka_1_out_12[6]));
  LED L59 (.in(general_mothafucka_1_out_12[5]));
  LED L67 (.in(general_mothafucka_1_out_13[5]));
  LED L66 (.in(general_mothafucka_1_out_13[6]));
  LED L65 (.in(general_mothafucka_1_out_13[7]));
  LED L73 (.in(general_mothafucka_1_out_14[7]));
  LED L75 (.in(general_mothafucka_1_out_14[5]));
  LED L74 (.in(general_mothafucka_1_out_14[6]));
  LED L4 (.in(general_mothafucka_1_out_7[4]));
  LED L5 (.in(general_mothafucka_1_out_7[3]));
  LED L16 (.in(general_mothafucka_1_out_8[3]));
  LED L15 (.in(general_mothafucka_1_out_8[4]));
  LED L26 (.in(general_mothafucka_1_out_9[4]));
  LED L27 (.in(general_mothafucka_1_out_9[3]));
  LED L37 (.in(general_mothafucka_1_out_10[4]));
  LED L38 (.in(general_mothafucka_1_out_10[3]));
  LED L49 (.in(general_mothafucka_1_out_11[4]));
  LED L50 (.in(general_mothafucka_1_out_11[3]));
  LED L61 (.in(general_mothafucka_1_out_12[3]));
  LED L60 (.in(general_mothafucka_1_out_12[4]));
  LED L68 (.in(general_mothafucka_1_out_13[4]));
  LED L69 (.in(general_mothafucka_1_out_13[3]));
  LED L76 (.in(general_mothafucka_1_out_14[3]));
  LED L75_2 (.in(general_mothafucka_1_out_14[4]));
  LED L8 (.in(general_mothafucka_1_out_7[0]));
  LED L6 (.in(general_mothafucka_1_out_7[2]));
  LED L7 (.in(general_mothafucka_1_out_7[1]));
  LED L17 (.in(general_mothafucka_1_out_8[2]));
  LED L18 (.in(general_mothafucka_1_out_8[1]));
  LED L19 (.in(general_mothafucka_1_out_8[0]));
  LED L29 (.in(general_mothafucka_1_out_9[1]));
  LED L30 (.in(general_mothafucka_1_out_9[0]));
  LED L28 (.in(general_mothafucka_1_out_9[2]));
  LED L40 (.in(general_mothafucka_1_out_10[1]));
  LED L41 (.in(general_mothafucka_1_out_10[0]));
  LED L39 (.in(general_mothafucka_1_out_10[2]));
  LED L53 (.in(general_mothafucka_1_out_11[0]));
  LED L51 (.in(general_mothafucka_1_out_11[2]));
  LED L52 (.in(general_mothafucka_1_out_11[1]));
  LED L64 (.in(general_mothafucka_1_out_12[0]));
  LED L63 (.in(general_mothafucka_1_out_12[1]));
  LED L62 (.in(general_mothafucka_1_out_12[2]));
  LED L70 (.in(general_mothafucka_1_out_13[2]));
  LED L72 (.in(general_mothafucka_1_out_13[0]));
  LED L71 (.in(general_mothafucka_1_out_13[1]));
  LED L78 (.in(general_mothafucka_1_out_14[1]));
  LED L77 (.in(general_mothafucka_1_out_14[2]));
  LED L79 (.in(general_mothafucka_1_out_14[0]));
  LED led_1 ();  // open: in
  LED led_2 ();  // open: in
  LED led_3 ();  // open: in
  LED led_4 ();  // open: in
  LED led_5 ();  // open: in
  LED led_6 ();  // open: in
  LED led_7 ();  // open: in
  LED led_8 ();  // open: in
  LED led_9 ();  // open: in
  LED led_10 ();  // open: in
  LED led_11 ();  // open: in
  LED led_12 ();  // open: in
  LED led_13 ();  // open: in
  LED led_14 ();  // open: in
  LED led_15 ();  // open: in
  LED led_16 ();  // open: in
  LED led_17 ();  // open: in
  LED led_18 ();  // open: in
  LED led_19 ();  // open: in
  LED led_20 ();  // open: in
  LED led_21 ();  // open: in
  LED led_22 ();  // open: in
  LED led_23 ();  // open: in
  LED led_24 ();  // open: in
endmodule

// code_button1
module code_button (
  input  g,
  input  d,
  input  h,
  input  b,
  output activ_button,
  output code_button1,
  output code_button2
);

  wire and_3_out, and_4_out, and_5_out, and_6_out, not_1_out, not_2_out, not_3_out, not_4_out, not_5_out,
       not_6_out, not_7_out, not_8_out, not_9_out, not_10_out, not_11_out, not_12_out, not_13_out,
       not_14_out, not_15_out, not_16_out;

  not not_1 (not_1_out, g);
  not not_2 (not_2_out, d);
  not not_3 (not_3_out, h);
  not not_4 (not_4_out, g);
  not not_5 (not_5_out, d);
  not not_6 (not_6_out, b);
  not not_7 (not_7_out, g);
  not not_8 (not_8_out, h);
  not not_9 (not_9_out, b);
  not not_10 (not_10_out, d);
  not not_11 (not_11_out, h);
  not not_12 (not_12_out, b);
  not not_13 (not_13_out, g);
  and and_1 (code_button1, not_13_out, not_14_out);
  not not_14 (not_14_out, d);
  not not_15 (not_15_out, g);
  and and_2 (code_button2, not_15_out, not_16_out);
  not not_16 (not_16_out, h);
  and and_3 (and_3_out, not_1_out, not_2_out, not_3_out, b);
  and and_4 (and_4_out, not_4_out, not_5_out, h, not_6_out);
  and and_5 (and_5_out, not_7_out, d, not_8_out, not_9_out);
  and and_6 (and_6_out, g, not_10_out, not_11_out, not_12_out);
  or or_1 (activ_button, and_3_out, and_4_out, and_5_out, and_6_out);
endmodule

// impulsion1
module impulsion (
  input  activ_button,
  input  code_button1,
  input  code_button2,
  input  memory_button1,
  input  memory_button2,
  output code_impulsion1,
  output code_impulsion2
);

  wire and_1_out, and_2_out, and_3_out, and_4_out, and_5_out, and_6_out, and_7_out, not_1_out, not_2_out,
       not_3_out, not_4_out, not_5_out, not_6_out;

  not not_1 (not_1_out, activ_button);
  not not_2 (not_2_out, activ_button);
  not not_3 (not_3_out, code_button1);
  not not_4 (not_4_out, memory_button1);
  not not_5 (not_5_out, code_button1);
  not not_6 (not_6_out, memory_button1);
  and and_1 (and_1_out, not_1_out, memory_button1);
  and and_2 (and_2_out, activ_button, code_button1);
  and and_3 (and_3_out, not_2_out, memory_button2);
  and and_4 (and_4_out, not_3_out, not_4_out, memory_button2);
  and and_5 (and_5_out, code_button1, memory_button1, memory_button2);
  and and_6 (and_6_out, activ_button, not_5_out, code_button2, memory_button1);
  and and_7 (and_7_out, activ_button, code_button1, code_button2, not_6_out);
  or or_1 (code_impulsion1, and_1_out, and_2_out);
  or or_2 (code_impulsion2, and_3_out, and_4_out, and_5_out, and_6_out, and_7_out);
endmodule

// treatment_impulsion2
module treatment_impulsion (
  input  g,
  input  d,
  input  h,
  input  b,
  input  clock,
  output impulsion1,
  output impulsion2
);

  wire code_button_1_activ_button, code_button_1_code_button1, code_button_1_code_button2, d_ff_1_q, d_ff_2_q;

  code_button code_button_1 (
    .g(g), .d(d), .h(h), .b(b), .activ_button(code_button_1_activ_button),
    .code_button1(code_button_1_code_button1), .code_button2(code_button_1_code_button2));
  impulsion impulsion_1 (
    .activ_button(code_button_1_activ_button), .code_button1(code_button_1_code_button1),
    .code_button2(code_button_1_code_button2), .memory_button1(d_ff_1_q), .memory_button2(d_ff_2_q),
    .code_impulsion1(impulsion1), .code_impulsion2(impulsion2));
  D_Flip_Flop d_ff_1 (.D(impulsion1), .clk(clock), .Q(d_ff_1_q));  // open: Qn, preset, reset
  D_Flip_Flop d_ff_2 (.D(impulsion2), .clk(clock), .Q(d_ff_2_q));  // open: Qn, preset, reset
endmodule

// decode_impulsion2
module decode_impulsion (
  input  impulsion1,
  input  impulsion2,
  output g,
  output d,
  output h,
  output b
);

  wire not_1_out, not_2_out, not_3_out, not_4_out;

  not not_1 (not_1_out, impulsion1);
  not not_2 (not_2_out, impulsion2);
  not not_3 (not_3_out, impulsion1);
  not not_4 (not_4_out, impulsion2);
  and and_1 (b, impulsion1, impulsion2);
  and and_2 (g, not_1_out, not_2_out);
  and and_3 (d, not_3_out, impulsion2);
  and and_4 (h, impulsion1, not_4_out);
endmodule

module general_snake (
  input  g,
  input  d,
  input  h,
  input  reset,
  input  b,
  input  clock,
  output [2:0] positionline,
  output [7:0] currentline,
  output [7:0] s1,
  output [7:0] s2,
  output [7:0] s3,
  output [7:0] s4,
  output [7:0] s5,
  output [7:0] s6,
  output [7:0] s7,
  output [7:0] s8,
  output reset_2
);

  wire decode_impulsion_1_b, decode_impulsion_1_d, decode_impulsion_1_g, decode_impulsion_1_h, or_1_out,
       or_2_out, or_3_out, or_4_out, or_5_out, or_6_out, or_7_out, or_8_out, sr_1_q, sr_2_q, sr_3_q, sr_4_q,
       treatment_impulsion_1_impulsion1, treatment_impulsion_1_impulsion2;

  or or_1 (or_1_out, d, h, b);
  or or_2 (or_2_out, g, h, b);
  or or_3 (or_3_out, g, d, h);
  SR sr_1 (.R(or_7_out), .S(d), .Q(sr_1_q));
  or or_4 (or_4_out, g, d, b);
  SR sr_2 (.R(or_5_out), .S(b), .Q(sr_2_q));
  or or_5 (or_5_out, or_3_out, reset);
  SR sr_3 (.R(or_8_out), .S(g), .Q(sr_3_q));
  SR sr_4 (.R(or_6_out), .S(h), .Q(sr_4_q));
  or or_6 (or_6_out, reset, or_4_out);
  or or_7 (or_7_out, or_2_out, reset);
  treatment_impulsion treatment_impulsion_1 (
    .g(sr_3_q), .d(sr_1_q), .h(sr_4_q), .b(sr_2_q), .clock(clock),
    .impulsion1(treatment_impulsion_1_impulsion1), .impulsion2(treatment_impulsion_1_impulsion2));
  or or_8 (or_8_out, reset, or_1_out);
  decode_impulsion decode_impulsion_1 (
    .impulsion1(treatment_impulsion_1_impulsion1), .impulsion2(treatment_impulsion_1_impulsion2),
    .g(decode_impulsion_1_g), .d(decode_impulsion_1_d), .h(decode_impulsion_1_h), .b(decode_impulsion_1_b));
  direction direction_1 (
    .reset(reset), .g(decode_impulsion_1_g), .d(decode_impulsion_1_d), .h(decode_impulsion_1_h),
    .b(decode_impulsion_1_b), .clock(clock), .position_line(positionline), .current_line(currentline),
    .reset_2(reset_2));
  graphiq_link graphiq_link_1 (
    .position(positionline), .line(currentline), .a(s1), .b(s2), .c(s3), .d(s4), .e(s5), .f(s6), .g(s7),
    .h(s8));
endmodule

// right1
module right (
  input  right_active,
  input  a,
  input  b,
  input  c,
  input  d,
  input  e,
  input  f,
  input  g,
  input  h,
  output A_2,
  output B_2,
  output C_2,
  output D_2,
  output E_2,
  output F_2,
  output G_2,
  output H_2,
  output RESET
);

  and and_1 (B_2, right_active, a);
  and and_2 (C_2, right_active, b);
  and and_3 (D_2, right_active, c);
  and and_4 (E_2, right_active, d);
  and and_5 (F_2, right_active, e);
  and and_6 (G_2, right_active, f);
  and and_7 (H_2, right_active, g);
  and and_8 (RESET, right_active, h);

  assign A_2 = 1'b0;
endmodule

// direction1
module direction (
  input  reset,
  input  g,
  input  d,
  input  h,
  input  b,
  input  clock,
  output [2:0] position_line,
  output [7:0] current_line,
  output reset_2
);

  wire left_1_reset, new_line_1_reset_2, or_1_out, right_1_reset;
  wire [7:0] and_1_out, and_2_out, left_1_h_2, matrix_creator_1_h, matrix_creator_2_h, or_2_out, or_3_out,
       right_1_h_2;

  or or_1 (or_1_out, left_1_reset, right_1_reset, new_line_1_reset_2);
  right right_1 (
    .right_active(d), .a(current_line[7]), .b(current_line[6]), .c(current_line[5]), .d(current_line[4]),
    .e(current_line[3]), .f(current_line[2]), .g(current_line[1]), .h(current_line[0]), .A_2(right_1_h_2[7]),
    .B_2(right_1_h_2[6]), .C_2(right_1_h_2[5]), .D_2(right_1_h_2[4]), .E_2(right_1_h_2[3]),
    .F_2(right_1_h_2[2]), .G_2(right_1_h_2[1]), .H_2(right_1_h_2[0]), .RESET(right_1_reset));
  new_line new_line_1 (
    .h(h), .b(b), .clock(clock), .reset(reset), .reset_2(new_line_1_reset_2), .l1(position_line[2]),
    .l2(position_line[1]), .l3(position_line[0]));
  left left_1 (
    .a(current_line[7]), .b(current_line[6]), .c(current_line[5]), .d(current_line[4]), .e(current_line[3]),
    .f(current_line[2]), .g(current_line[1]), .h(current_line[0]), .LEFT_ACTIVE(g), .A_2(left_1_h_2[7]),
    .B_2(left_1_h_2[6]), .C_2(left_1_h_2[5]), .D_2(left_1_h_2[4]), .E_2(left_1_h_2[3]), .F_2(left_1_h_2[2]),
    .G_2(left_1_h_2[1]), .H_2(left_1_h_2[0]), .RESET(left_1_reset));
  matrix_creator matrix_creator_1 (
    .A(h), .a_2(matrix_creator_1_h[7]), .b(matrix_creator_1_h[6]), .c(matrix_creator_1_h[5]),
    .d(matrix_creator_1_h[4]), .e(matrix_creator_1_h[3]), .f(matrix_creator_1_h[2]),
    .g(matrix_creator_1_h[1]), .h(matrix_creator_1_h[0]));
  matrix_creator matrix_creator_2 (
    .A(b), .a_2(matrix_creator_2_h[7]), .b(matrix_creator_2_h[6]), .c(matrix_creator_2_h[5]),
    .d(matrix_creator_2_h[4]), .e(matrix_creator_2_h[3]), .f(matrix_creator_2_h[2]),
    .g(matrix_creator_2_h[1]), .h(matrix_creator_2_h[0]));
  D_Flip_Flop d_ff_1 (.D(or_1_out), .clk(clock), .Q(reset_2));  // open: Qn, preset, reset
  assign or_2_out = right_1_h_2 | left_1_h_2;  // OR_Gate or_2, 8 bits wide
  assign and_1_out = current_line & matrix_creator_2_h;  // AND_Gate and_1, 8 bits wide
  assign and_2_out = current_line & matrix_creator_1_h;  // AND_Gate and_2, 8 bits wide
  D_Flip_Flop d_ff_2 (.D(or_3_out[7]), .clk(clock), .Q(current_line[7]), .reset(reset));  // open: Qn, preset
  D_Flip_Flop d_ff_3 (.D(or_3_out[6]), .clk(clock), .Q(current_line[6]), .reset(reset));  // open: Qn, preset
  D_Flip_Flop d_ff_4 (.D(or_3_out[5]), .clk(clock), .Q(current_line[5]), .reset(reset));  // open: Qn, preset
  D_Flip_Flop d_ff_5 (.D(or_3_out[4]), .clk(clock), .Q(current_line[4]), .preset(reset));  // open: Qn, reset
  assign or_3_out = or_2_out | and_2_out | and_1_out;  // OR_Gate or_3, 8 bits wide
  D_Flip_Flop d_ff_6 (.D(or_3_out[3]), .clk(clock), .Q(current_line[3]), .reset(reset));  // open: Qn, preset
  D_Flip_Flop d_ff_7 (.D(or_3_out[2]), .clk(clock), .Q(current_line[2]), .reset(reset));  // open: Qn, preset
  D_Flip_Flop d_ff_8 (.D(or_3_out[1]), .clk(clock), .Q(current_line[1]), .reset(reset));  // open: Qn, preset
  D_Flip_Flop d_ff_9 (.D(or_3_out[0]), .clk(clock), .Q(current_line[0]), .reset(reset));  // open: Qn, preset
endmodule

// left1
module left (
  input  a,
  input  b,
  input  c,
  input  d,
  input  e,
  input  f,
  input  g,
  input  h,
  input  LEFT_ACTIVE,
  output A_2,
  output B_2,
  output C_2,
  output D_2,
  output E_2,
  output F_2,
  output G_2,
  output H_2,
  output RESET
);

  and and_1 (A_2, LEFT_ACTIVE, b);
  and and_2 (B_2, LEFT_ACTIVE, c);
  and and_3 (C_2, LEFT_ACTIVE, d);
  and and_4 (D_2, LEFT_ACTIVE, e);
  and and_5 (E_2, LEFT_ACTIVE, f);
  and and_6 (F_2, LEFT_ACTIVE, g);
  and and_7 (G_2, LEFT_ACTIVE, h);
  and and_8 (RESET, LEFT_ACTIVE, a);

  assign H_2 = 1'b0;
endmodule

// matrix_creator1
module matrix_creator (
  input  A,
  output a_2,
  output b,
  output c,
  output d,
  output e,
  output f,
  output g,
  output h
);


  assign a_2 = A;
  assign b = A;
  assign c = A;
  assign d = A;
  assign e = A;
  assign f = A;
  assign g = A;
  assign h = A;
endmodule

module memory_line (
  input  reset,
  input  h,
  input  b,
  input  l1,
  input  l2,
  input  l3,
  output L1_2,
  output L2_2,
  output L3_2,
  output reset_2
);

  wire and_1_out, and_2_out, and_3_out, and_4_out, and_5_out, and_6_out, and_7_out, and_8_out, and_9_out,
       and_10_out, and_11_out, and_12_out, and_13_out, and_14_out, and_15_out, not_1_out, not_2_out,
       not_3_out, not_4_out, not_5_out, not_6_out, not_7_out, not_8_out, not_9_out, not_10_out, not_11_out,
       not_12_out, not_13_out, not_14_out, not_15_out, not_16_out, not_17_out, not_18_out, not_19_out,
       not_20_out, not_21_out, not_22_out, not_23_out, not_24_out, not_25_out, not_26_out, not_27_out,
       not_28_out, not_29_out;

  not not_1 (not_1_out, reset);
  not not_2 (not_2_out, h);
  not not_3 (not_3_out, l2);
  not not_4 (not_4_out, reset);
  not not_5 (not_5_out, h);
  not not_6 (not_6_out, l3);
  not not_7 (not_7_out, reset);
  not not_8 (not_8_out, b);
  not not_9 (not_9_out, reset);
  not not_10 (not_10_out, b);
  not not_11 (not_11_out, reset);
  not not_12 (not_12_out, l1);
  not not_13 (not_13_out, h);
  not not_14 (not_14_out, b);
  not not_15 (not_15_out, h);
  not not_16 (not_16_out, l3);
  not not_17 (not_17_out, b);
  not not_18 (not_18_out, l2);
  not not_19 (not_19_out, l2);
  not not_20 (not_20_out, l3);
  not not_21 (not_21_out, h);
  not not_22 (not_22_out, b);
  not not_23 (not_23_out, l3);
  not not_24 (not_24_out, l3);
  not not_25 (not_25_out, reset);
  not not_26 (not_26_out, reset);
  not not_27 (not_27_out, l1);
  not not_28 (not_28_out, l2);
  not not_29 (not_29_out, l3);
  and and_1 (and_1_out, not_1_out, not_2_out, l1, not_3_out);
  and and_2 (and_2_out, not_4_out, not_5_out, l1, not_6_out);
  and and_3 (and_3_out, not_7_out, not_8_out, l1, l3);
  and and_4 (and_4_out, not_9_out, not_10_out, l1, l2);
  and and_5 (and_5_out, not_11_out, b, not_12_out, l2, l3);
  and and_6 (and_6_out, not_13_out, not_14_out, l2);
  and and_7 (and_7_out, not_15_out, l2, not_16_out);
  and and_8 (and_8_out, not_17_out, l2, l3);
  and and_9 (and_9_out, b, not_18_out, l3);
  and and_10 (and_10_out, h, not_19_out, not_20_out);
  and and_11 (and_11_out, not_21_out, not_22_out, l3);
  and and_12 (and_12_out, b, not_23_out);
  and and_13 (and_13_out, h, not_24_out);
  and and_14 (and_14_out, not_25_out, b, l1, l2, l3);
  and and_15 (and_15_out, not_26_out, h, not_27_out, not_28_out, not_29_out);
  or or_1 (L1_2, and_1_out, and_2_out, and_3_out, and_4_out, and_5_out);
  or or_2 (L2_2, and_6_out, and_7_out, and_8_out, and_9_out, and_10_out, reset);
  or or_3 (L3_2, and_11_out, and_12_out, and_13_out, reset);
  or or_4 (reset_2, and_14_out, and_15_out);
endmodule

// new_line1
module new_line (
  input  h,
  input  b,
  input  clock,
  input  reset,
  output reset_2,
  output l1,
  output l2,
  output l3
);

  wire memory_line_1_l1_2, memory_line_1_l2_2, memory_line_1_l3_2;

  memory_line memory_line_1 (
    .reset(reset), .h(h), .b(b), .l1(l1), .l2(l2), .l3(l3), .L1_2(memory_line_1_l1_2),
    .L2_2(memory_line_1_l2_2), .L3_2(memory_line_1_l3_2), .reset_2(reset_2));
  D_Flip_Flop d_ff_1 (.D(memory_line_1_l1_2), .clk(clock), .Q(l1), .reset(reset));  // open: Qn, preset
  D_Flip_Flop d_ff_2 (.D(memory_line_1_l2_2), .clk(clock), .Q(l2), .preset(reset));  // open: Qn, reset
  D_Flip_Flop d_ff_3 (.D(memory_line_1_l3_2), .clk(clock), .Q(l3), .preset(reset));  // open: Qn, reset
endmodule

// graphiq_link1
module graphiq_link (
  input  [2:0] position,
  input  [7:0] line,
  output [7:0] a,
  output [7:0] b,
  output [7:0] c,
  output [7:0] d,
  output [7:0] e,
  output [7:0] f,
  output [7:0] g,
  output [7:0] h
);

  graphique_link5 graphique_link5_1 (
    .l1(position[0]), .l2(position[1]), .l3(position[2]), .a(line[0]), .b(line[1]), .c(line[2]), .d(line[3]),
    .e(line[4]), .f(line[5]), .g(line[6]), .h(line[7]), .A_2(b[0]), .B_2(b[1]), .C_2(b[2]), .D_2(b[3]),
    .E_2(b[4]), .F_2(b[5]), .G_2(b[6]), .H_2(b[7]));
  graphique_link1 graphique_link1_1 (
    .l1(position[0]), .l2(position[1]), .l3(position[2]), .a(line[0]), .b(line[1]), .c(line[2]), .d(line[3]),
    .e(line[4]), .f(line[5]), .g(line[6]), .h(line[7]), .A_2(a[0]), .B_2(a[1]), .C_2(a[2]), .D_2(a[3]),
    .E_2(a[4]), .F_2(a[5]), .G_2(a[6]), .H_2(a[7]));
  graphique_link7 graphique_link7_1 (
    .l1(position[2]), .l2(position[1]), .l3(position[0]), .a(line[0]), .b(line[1]), .c(line[2]), .d(line[3]),
    .e(line[4]), .f(line[5]), .g(line[6]), .h(line[7]), .A_2(f[0]), .B_2(f[1]), .C_2(f[2]), .D_2(f[3]),
    .E_2(f[4]), .F_2(f[5]), .G_2(f[6]), .H_2(f[7]));
  graphique_link2 graphique_link2_1 (
    .l1(position[0]), .l2(position[1]), .l3(position[2]), .a(line[0]), .b(line[1]), .c(line[2]), .d(line[3]),
    .e(line[4]), .f(line[5]), .g(line[6]), .h(line[7]), .A_2(e[0]), .B_2(e[1]), .C_2(e[2]), .D_2(e[3]),
    .E_2(e[4]), .F_2(e[5]), .G_2(e[6]), .H_2(e[7]));
  graphique_link3 graphique_link3_1 (
    .l1(position[0]), .l2(position[1]), .l3(position[2]), .a(line[0]), .b(line[1]), .c(line[2]), .d(line[3]),
    .e(line[4]), .f(line[5]), .g(line[6]), .h(line[7]), .A_2(c[0]), .B_2(c[1]), .C_2(c[2]), .D_2(c[3]),
    .E_2(c[4]), .F_2(c[5]), .G_2(c[6]), .H_2(c[7]));
  graphique_link4 graphique_link4_1 (
    .l1(position[2]), .l2(position[1]), .l3(position[0]), .a(line[0]), .b(line[1]), .c(line[2]), .d(line[3]),
    .e(line[4]), .f(line[5]), .g(line[6]), .h(line[7]), .A_2(g[0]), .B_2(g[1]), .C_2(g[2]), .D_2(g[3]),
    .E_2(g[4]), .F_2(g[5]), .G_2(g[6]), .H_2(g[7]));
  graphique_link8 graphique_link8_1 (
    .l1(position[2]), .l2(position[1]), .l3(position[0]), .a(line[0]), .b(line[1]), .c(line[2]), .d(line[3]),
    .e(line[4]), .f(line[5]), .g(line[6]), .h(line[7]), .A_2(h[0]), .B_2(h[1]), .C_2(h[2]), .D_2(h[3]),
    .E_2(h[4]), .F_2(h[5]), .G_2(h[6]), .H_2(h[7]));
  graphique_link6 graphique_link6_1 (
    .l1(position[2]), .l2(position[1]), .l3(position[0]), .a(line[0]), .b(line[1]), .c(line[2]), .d(line[3]),
    .e(line[4]), .f(line[5]), .g(line[6]), .h(line[7]), .A_2(d[0]), .B_2(d[1]), .C_2(d[2]), .D_2(d[3]),
    .E_2(d[4]), .F_2(d[5]), .G_2(d[6]), .H_2(d[7]));
endmodule

module graphique_link1 (
  input  l1,
  input  l2,
  input  l3,
  input  a,
  input  b,
  input  c,
  input  d,
  input  e,
  input  f,
  input  g,
  input  h,
  output A_2,
  output B_2,
  output C_2,
  output D_2,
  output E_2,
  output F_2,
  output G_2,
  output H_2
);

  wire not_1_out, not_2_out, not_3_out, not_4_out, not_5_out, not_6_out, not_7_out, not_8_out, not_9_out,
       not_10_out, not_11_out, not_12_out, not_13_out, not_14_out, not_15_out, not_16_out, not_17_out,
       not_18_out, not_19_out, not_20_out, not_21_out, not_22_out, not_23_out, not_24_out;

  not not_1 (not_1_out, l1);
  not not_2 (not_2_out, l2);
  not not_3 (not_3_out, l3);
  not not_4 (not_4_out, l1);
  not not_5 (not_5_out, l2);
  not not_6 (not_6_out, l3);
  not not_7 (not_7_out, l1);
  not not_8 (not_8_out, l2);
  not not_9 (not_9_out, l3);
  not not_10 (not_10_out, l1);
  not not_11 (not_11_out, l2);
  not not_12 (not_12_out, l3);
  not not_13 (not_13_out, l1);
  not not_14 (not_14_out, l2);
  not not_15 (not_15_out, l3);
  not not_16 (not_16_out, l1);
  not not_17 (not_17_out, l2);
  not not_18 (not_18_out, l3);
  not not_19 (not_19_out, l1);
  not not_20 (not_20_out, l2);
  not not_21 (not_21_out, l3);
  not not_22 (not_22_out, l1);
  not not_23 (not_23_out, l2);
  not not_24 (not_24_out, l3);
  and and_1 (A_2, not_1_out, not_2_out, not_3_out, a);
  and and_2 (B_2, not_4_out, not_5_out, not_6_out, b);
  and and_3 (C_2, not_7_out, not_8_out, not_9_out, c);
  and and_4 (D_2, not_10_out, not_11_out, not_12_out, d);
  and and_5 (E_2, not_13_out, not_14_out, not_15_out, e);
  and and_6 (F_2, not_16_out, not_17_out, not_18_out, f);
  and and_7 (G_2, not_19_out, not_20_out, not_21_out, g);
  and and_8 (H_2, not_22_out, not_23_out, not_24_out, h);
endmodule

module graphique_link2 (
  input  l1,
  input  l2,
  input  l3,
  input  a,
  input  b,
  input  c,
  input  d,
  input  e,
  input  f,
  input  g,
  input  h,
  output A_2,
  output B_2,
  output C_2,
  output D_2,
  output E_2,
  output F_2,
  output G_2,
  output H_2
);

  wire not_1_out, not_2_out, not_3_out, not_4_out, not_5_out, not_6_out, not_7_out, not_8_out, not_9_out,
       not_10_out, not_11_out, not_12_out, not_13_out, not_14_out, not_15_out, not_16_out;

  not not_1 (not_1_out, l1);
  not not_2 (not_2_out, l2);
  not not_3 (not_3_out, l1);
  not not_4 (not_4_out, l2);
  not not_5 (not_5_out, l1);
  not not_6 (not_6_out, l2);
  not not_7 (not_7_out, l1);
  not not_8 (not_8_out, l2);
  not not_9 (not_9_out, l1);
  not not_10 (not_10_out, l2);
  not not_11 (not_11_out, l1);
  not not_12 (not_12_out, l2);
  not not_13 (not_13_out, l1);
  not not_14 (not_14_out, l2);
  not not_15 (not_15_out, l1);
  not not_16 (not_16_out, l2);
  and and_1 (A_2, not_1_out, not_2_out, l3, a);
  and and_2 (B_2, not_3_out, not_4_out, l3, b);
  and and_3 (C_2, not_5_out, not_6_out, l3, c);
  and and_4 (D_2, not_7_out, not_8_out, l3, d);
  and and_5 (E_2, not_9_out, not_10_out, l3, e);
  and and_6 (F_2, not_11_out, not_12_out, l3, f);
  and and_7 (G_2, not_13_out, not_14_out, l3, g);
  and and_8 (H_2, not_15_out, not_16_out, l3, h);
endmodule

module graphique_link3 (
  input  l1,
  input  l2,
  input  l3,
  input  a,
  input  b,
  input  c,
  input  d,
  input  e,
  input  f,
  input  g,
  input  h,
  output A_2,
  output B_2,
  output C_2,
  output D_2,
  output E_2,
  output F_2,
  output G_2,
  output H_2
);

  wire not_1_out, not_2_out, not_3_out, not_4_out, not_5_out, not_6_out, not_7_out, not_8_out, not_9_out,
       not_10_out, not_11_out, not_12_out, not_13_out, not_14_out, not_15_out, not_16_out;

  not not_1 (not_1_out, l1);
  not not_2 (not_2_out, l3);
  not not_3 (not_3_out, l1);
  not not_4 (not_4_out, l3);
  not not_5 (not_5_out, l1);
  not not_6 (not_6_out, l3);
  not not_7 (not_7_out, l1);
  not not_8 (not_8_out, l3);
  not not_9 (not_9_out, l1);
  not not_10 (not_10_out, l3);
  not not_11 (not_11_out, l1);
  not not_12 (not_12_out, l3);
  not not_13 (not_13_out, l1);
  not not_14 (not_14_out, l3);
  not not_15 (not_15_out, l1);
  not not_16 (not_16_out, l3);
  and and_1 (A_2, not_1_out, l2, not_2_out, a);
  and and_2 (B_2, not_3_out, l2, not_4_out, b);
  and and_3 (C_2, not_5_out, l2, not_6_out, c);
  and and_4 (D_2, not_7_out, l2, not_8_out, d);
  and and_5 (E_2, not_9_out, l2, not_10_out, e);
  and and_6 (F_2, not_11_out, l2, not_12_out, f);
  and and_7 (G_2, not_13_out, l2, not_14_out, g);
  and and_8 (H_2, not_15_out, l2, not_16_out, h);
endmodule

module graphique_link4 (
  input  l1,
  input  l2,
  input  l3,
  input  a,
  input  b,
  input  c,
  input  d,
  input  e,
  input  f,
  input  g,
  input  h,
  output A_2,
  output B_2,
  output C_2,
  output D_2,
  output E_2,
  output F_2,
  output G_2,
  output H_2
);

  wire not_1_out, not_2_out, not_3_out, not_4_out, not_5_out, not_6_out, not_7_out, not_8_out;

  not not_1 (not_1_out, l3);
  not not_2 (not_2_out, l3);
  not not_3 (not_3_out, l3);
  not not_4 (not_4_out, l3);
  not not_5 (not_5_out, l3);
  not not_6 (not_6_out, l3);
  not not_7 (not_7_out, l3);
  not not_8 (not_8_out, l3);
  and and_1 (A_2, l1, l2, not_1_out, a);
  and and_2 (B_2, l1, l2, not_2_out, b);
  and and_3 (C_2, l1, l2, not_3_out, c);
  and and_4 (D_2, l1, l2, not_4_out, d);
  and and_5 (E_2, l1, l2, not_5_out, e);
  and and_6 (F_2, l1, l2, not_6_out, f);
  and and_7 (G_2, l1, l2, not_7_out, g);
  and and_8 (H_2, l1, l2, not_8_out, h);
endmodule

module graphique_link5 (
  input  l1,
  input  l2,
  input  l3,
  input  a,
  input  b,
  input  c,
  input  d,
  input  e,
  input  f,
  input  g,
  input  h,
  output A_2,
  output B_2,
  output C_2,
  output D_2,
  output E_2,
  output F_2,
  output G_2,
  output H_2
);

  wire not_1_out, not_2_out, not_3_out, not_4_out, not_5_out, not_6_out, not_7_out, not_8_out, not_9_out,
       not_10_out, not_11_out, not_12_out, not_13_out, not_14_out, not_15_out, not_16_out;

  not not_1 (not_1_out, l2);
  not not_2 (not_2_out, l3);
  not not_3 (not_3_out, l2);
  not not_4 (not_4_out, l3);
  not not_5 (not_5_out, l2);
  not not_6 (not_6_out, l3);
  not not_7 (not_7_out, l2);
  not not_8 (not_8_out, l3);
  not not_9 (not_9_out, l2);
  not not_10 (not_10_out, l3);
  not not_11 (not_11_out, l2);
  not not_12 (not_12_out, l3);
  not not_13 (not_13_out, l2);
  not not_14 (not_14_out, l3);
  not not_15 (not_15_out, l2);
  not not_16 (not_16_out, l3);
  and and_1 (A_2, l1, not_1_out, not_2_out, a);
  and and_2 (B_2, l1, not_3_out, not_4_out, b);
  and and_3 (C_2, l1, not_5_out, not_6_out, c);
  and and_4 (D_2, l1, not_7_out, not_8_out, d);
  and and_5 (E_2, l1, not_9_out, not_10_out, e);
  and and_6 (F_2, l1, not_11_out, not_12_out, f);
  and and_7 (G_2, l1, not_13_out, not_14_out, g);
  and and_8 (H_2, l1, not_15_out, not_16_out, h);
endmodule

module graphique_link6 (
  input  l1,
  input  l2,
  input  l3,
  input  a,
  input  b,
  input  c,
  input  d,
  input  e,
  input  f,
  input  g,
  input  h,
  output A_2,
  output B_2,
  output C_2,
  output D_2,
  output E_2,
  output F_2,
  output G_2,
  output H_2
);

  wire not_1_out, not_2_out, not_3_out, not_4_out, not_5_out, not_6_out, not_7_out, not_8_out;

  not not_1 (not_1_out, l1);
  not not_2 (not_2_out, l1);
  not not_3 (not_3_out, l1);
  not not_4 (not_4_out, l1);
  not not_5 (not_5_out, l1);
  not not_6 (not_6_out, l1);
  not not_7 (not_7_out, l1);
  not not_8 (not_8_out, l1);
  and and_1 (A_2, not_1_out, l2, l3, a);
  and and_2 (B_2, not_2_out, l2, l3, b);
  and and_3 (C_2, not_3_out, l2, l3, c);
  and and_4 (D_2, not_4_out, l2, l3, d);
  and and_5 (E_2, not_5_out, l2, l3, e);
  and and_6 (F_2, not_6_out, l2, l3, f);
  and and_7 (G_2, not_7_out, l2, l3, g);
  and and_8 (H_2, not_8_out, l2, l3, h);
endmodule

module graphique_link7 (
  input  l1,
  input  l2,
  input  l3,
  input  a,
  input  b,
  input  c,
  input  d,
  input  e,
  input  f,
  input  g,
  input  h,
  output A_2,
  output B_2,
  output C_2,
  output D_2,
  output E_2,
  output F_2,
  output G_2,
  output H_2
);

  wire not_1_out, not_2_out, not_3_out, not_4_out, not_5_out, not_6_out, not_7_out, not_8_out;

  not not_1 (not_1_out, l2);
  not not_2 (not_2_out, l2);
  not not_3 (not_3_out, l2);
  not not_4 (not_4_out, l2);
  not not_5 (not_5_out, l2);
  not not_6 (not_6_out, l2);
  not not_7 (not_7_out, l2);
  not not_8 (not_8_out, l2);
  and and_1 (A_2, l1, not_1_out, l3, a);
  and and_2 (B_2, l1, not_2_out, l3, b);
  and and_3 (C_2, l1, not_3_out, l3, c);
  and and_4 (D_2, l1, not_4_out, l3, d);
  and and_5 (E_2, l1, not_5_out, l3, e);
  and and_6 (F_2, l1, not_6_out, l3, f);
  and and_7 (G_2, l1, not_7_out, l3, g);
  and and_8 (H_2, l1, not_8_out, l3, h);
endmodule

module graphique_link8 (
  input  l1,
  input  l2,
  input  l3,
  input  a,
  input  b,
  input  c,
  input  d,
  input  e,
  input  f,
  input  g,
  input  h,
  output A_2,
  output B_2,
  output C_2,
  output D_2,
  output E_2,
  output F_2,
  output G_2,
  output H_2
);

  and and_1 (A_2, l1, l2, l3, a);
  and and_2 (B_2, l1, l2, l3, b);
  and and_3 (C_2, l1, l2, l3, c);
  and and_4 (D_2, l1, l2, l3, d);
  and and_5 (E_2, l1, l2, l3, e);
  and and_6 (F_2, l1, l2, l3, f);
  and and_7 (G_2, l1, l2, l3, g);
  and and_8 (H_2, l1, l2, l3, h);
endmodule

// SR1
module SR (
  input  R,
  input  S,
  output Q
);

  wire nor_2_out;

  nor nor_1 (Q, R, nor_2_out);
  nor nor_2 (nor_2_out, Q, S);
endmodule

module general_mushroomn (
  input  pos1,
  input  pos2,
  input  pos3,
  input  pos4,
  input  pos5,
  input  pos6,
  input  pos7,
  input  pos8,
  output [7:0] out_9,
  output [7:0] out_10,
  output [7:0] out_11,
  output [7:0] out_12,
  output [7:0] out_13,
  output [7:0] out_14,
  output [7:0] out_15,
  output [7:0] out_16,
  output [7:0] line_pos7,
  output [7:0] line_pos3,
  output [7:0] line_pos6,
  output [7:0] line_pos2,
  output [7:0] line_pos5,
  output [7:0] line_pos1,
  output [7:0] line_pos4,
  output [7:0] line_pos8
);

  wire [7:0] matrix_creator_1_a_2, matrix_creator_2_a_2, matrix_creator_3_a_2, matrix_creator_4_a_2,
       matrix_creator_5_a_2, matrix_creator_6_a_2, matrix_creator_7_a_2, matrix_creator_8_a_2;

  matrix_creator matrix_creator_1 (
    .A(pos8), .a_2(matrix_creator_1_a_2[0]), .b(matrix_creator_1_a_2[1]), .c(matrix_creator_1_a_2[2]),
    .d(matrix_creator_1_a_2[3]), .e(matrix_creator_1_a_2[4]), .f(matrix_creator_1_a_2[5]),
    .g(matrix_creator_1_a_2[6]), .h(matrix_creator_1_a_2[7]));
  matrix_creator matrix_creator_2 (
    .A(pos6), .a_2(matrix_creator_2_a_2[0]), .b(matrix_creator_2_a_2[1]), .c(matrix_creator_2_a_2[2]),
    .d(matrix_creator_2_a_2[3]), .e(matrix_creator_2_a_2[4]), .f(matrix_creator_2_a_2[5]),
    .g(matrix_creator_2_a_2[6]), .h(matrix_creator_2_a_2[7]));
  assign out_13 = matrix_creator_1_a_2 & 8'h1;  // AND_Gate and_1, 8 bits wide
  matrix_creator matrix_creator_3 (
    .A(pos7), .a_2(matrix_creator_3_a_2[0]), .b(matrix_creator_3_a_2[1]), .c(matrix_creator_3_a_2[2]),
    .d(matrix_creator_3_a_2[3]), .e(matrix_creator_3_a_2[4]), .f(matrix_creator_3_a_2[5]),
    .g(matrix_creator_3_a_2[6]), .h(matrix_creator_3_a_2[7]));
  matrix_creator matrix_creator_4 (
    .A(pos4), .a_2(matrix_creator_4_a_2[0]), .b(matrix_creator_4_a_2[1]), .c(matrix_creator_4_a_2[2]),
    .d(matrix_creator_4_a_2[3]), .e(matrix_creator_4_a_2[4]), .f(matrix_creator_4_a_2[5]),
    .g(matrix_creator_4_a_2[6]), .h(matrix_creator_4_a_2[7]));
  assign out_9 = matrix_creator_2_a_2 & 8'h80;  // AND_Gate and_2, 8 bits wide
  assign out_10 = matrix_creator_3_a_2 & 8'h80;  // AND_Gate and_3, 8 bits wide
  assign out_12 = matrix_creator_4_a_2 & 8'h8;  // AND_Gate and_4, 8 bits wide
  matrix_creator matrix_creator_5 (
    .A(pos2), .a_2(matrix_creator_5_a_2[0]), .b(matrix_creator_5_a_2[1]), .c(matrix_creator_5_a_2[2]),
    .d(matrix_creator_5_a_2[3]), .e(matrix_creator_5_a_2[4]), .f(matrix_creator_5_a_2[5]),
    .g(matrix_creator_5_a_2[6]), .h(matrix_creator_5_a_2[7]));
  matrix_creator matrix_creator_6 (
    .A(pos1), .a_2(matrix_creator_6_a_2[0]), .b(matrix_creator_6_a_2[1]), .c(matrix_creator_6_a_2[2]),
    .d(matrix_creator_6_a_2[3]), .e(matrix_creator_6_a_2[4]), .f(matrix_creator_6_a_2[5]),
    .g(matrix_creator_6_a_2[6]), .h(matrix_creator_6_a_2[7]));
  assign out_11 = matrix_creator_5_a_2 & 8'h10;  // AND_Gate and_5, 8 bits wide
  matrix_creator matrix_creator_7 (
    .A(pos5), .a_2(matrix_creator_7_a_2[0]), .b(matrix_creator_7_a_2[1]), .c(matrix_creator_7_a_2[2]),
    .d(matrix_creator_7_a_2[3]), .e(matrix_creator_7_a_2[4]), .f(matrix_creator_7_a_2[5]),
    .g(matrix_creator_7_a_2[6]), .h(matrix_creator_7_a_2[7]));
  assign out_15 = matrix_creator_6_a_2 & 8'h4;  // AND_Gate and_6, 8 bits wide
  matrix_creator matrix_creator_8 (
    .A(pos3), .a_2(matrix_creator_8_a_2[0]), .b(matrix_creator_8_a_2[1]), .c(matrix_creator_8_a_2[2]),
    .d(matrix_creator_8_a_2[3]), .e(matrix_creator_8_a_2[4]), .f(matrix_creator_8_a_2[5]),
    .g(matrix_creator_8_a_2[6]), .h(matrix_creator_8_a_2[7]));
  assign out_16 = matrix_creator_8_a_2 & 8'h40;  // AND_Gate and_7, 8 bits wide
  assign out_14 = matrix_creator_7_a_2 & 8'h10;  // AND_Gate and_8, 8 bits wide

  assign line_pos1 = 8'h4;
  assign line_pos2 = 8'h10;
  assign line_pos3 = 8'h40;
  assign line_pos4 = 8'h8;
  assign line_pos5 = 8'h10;
  assign line_pos6 = 8'h80;
  assign line_pos7 = 8'h80;
  assign line_pos8 = 8'h1;
endmodule

module general_mushroom_and_snake (
  input  g,
  input  d,
  input  h,
  input  b,
  input  reset,
  input  clock,
  output [7:0] s1,
  output [7:0] s2,
  output [7:0] s3,
  output [7:0] s4,
  output [7:0] s5,
  output [7:0] s6,
  output [7:0] s7,
  output [7:0] s8,
  output [7:0] ms1,
  output [7:0] out_16,
  output [7:0] out_17,
  output [7:0] out_18,
  output [7:0] out_19,
  output [7:0] out_20,
  output [7:0] out_21,
  output [7:0] out_22,
  output [2:0] position_line,
  output [7:0] current_line,
  output conditon1,
  output reset_2
);

  wire [7:0] general_mushroomn_1_line_pos1, general_mushroomn_1_line_pos2, general_mushroomn_1_line_pos3,
       general_mushroomn_1_line_pos4, general_mushroomn_1_line_pos5, general_mushroomn_1_line_pos6,
       general_mushroomn_1_line_pos7, general_mushroomn_1_line_pos8, general_mushroomn_1_out_9,
       general_mushroomn_1_out_10, general_mushroomn_1_out_11, general_mushroomn_1_out_12,
       general_mushroomn_1_out_13, general_mushroomn_1_out_14, general_mushroomn_1_out_15,
       general_mushroomn_1_out_16, memorize_pos_1_out_3, next_mushroom_1_pos;

  general_mushroomn general_mushroomn_1 (
    .pos1(memorize_pos_1_out_3[7]), .pos2(memorize_pos_1_out_3[6]), .pos3(memorize_pos_1_out_3[5]),
    .pos4(memorize_pos_1_out_3[4]), .pos5(memorize_pos_1_out_3[3]), .pos6(memorize_pos_1_out_3[2]),
    .pos7(memorize_pos_1_out_3[1]), .pos8(memorize_pos_1_out_3[0]), .out_9(general_mushroomn_1_out_9),
    .out_10(general_mushroomn_1_out_10), .out_11(general_mushroomn_1_out_11),
    .out_12(general_mushroomn_1_out_12), .out_13(general_mushroomn_1_out_13),
    .out_14(general_mushroomn_1_out_14), .out_15(general_mushroomn_1_out_15),
    .out_16(general_mushroomn_1_out_16), .line_pos7(general_mushroomn_1_line_pos7),
    .line_pos3(general_mushroomn_1_line_pos3), .line_pos6(general_mushroomn_1_line_pos6),
    .line_pos2(general_mushroomn_1_line_pos2), .line_pos5(general_mushroomn_1_line_pos5),
    .line_pos1(general_mushroomn_1_line_pos1), .line_pos4(general_mushroomn_1_line_pos4),
    .line_pos8(general_mushroomn_1_line_pos8));
  general_snake general_snake_1 (
    .g(g), .d(d), .h(h), .reset(reset), .b(b), .clock(clock), .positionline(position_line),
    .currentline(current_line), .s1(s1), .s2(s2), .s3(s3), .s4(s4), .s5(s5), .s6(s6), .s7(s7), .s8(s8),
    .reset_2(reset_2));
  next_mushroom next_mushroom_1 (
    .positionline(position_line), .currentline(current_line), .in_3(memorize_pos_1_out_3),
    .line_pos1(general_mushroomn_1_line_pos1), .line_pos2(general_mushroomn_1_line_pos2),
    .line_pos3(general_mushroomn_1_line_pos3), .linepos4(general_mushroomn_1_line_pos4),
    .linepos5(general_mushroomn_1_line_pos5), .linepos6(general_mushroomn_1_line_pos6),
    .linepos7(general_mushroomn_1_line_pos7), .linepos8(general_mushroomn_1_line_pos8),
    .condition_snake_is_on_mushrrom(conditon1), .pos(next_mushroom_1_pos));
  assign ms1 = s1 | general_mushroomn_1_out_9;  // OR_Gate or_1, 8 bits wide
  assign out_16 = s2 | general_mushroomn_1_out_10;  // OR_Gate or_2, 8 bits wide
  assign out_17 = s3 | general_mushroomn_1_out_11;  // OR_Gate or_3, 8 bits wide
  assign out_18 = s4 | general_mushroomn_1_out_12;  // OR_Gate or_4, 8 bits wide
  assign out_19 = s5 | general_mushroomn_1_out_13;  // OR_Gate or_5, 8 bits wide
  assign out_20 = s6 | general_mushroomn_1_out_14;  // OR_Gate or_6, 8 bits wide
  assign out_21 = s7 | general_mushroomn_1_out_15;  // OR_Gate or_7, 8 bits wide
  assign out_22 = s8 | general_mushroomn_1_out_16;  // OR_Gate or_8, 8 bits wide
  memorize_pos memorize_pos_1 (.reset(reset), .pos(next_mushroom_1_pos), .out_3(memorize_pos_1_out_3));
endmodule

module condition_snakeisonmushroom (
  input  [2:0] line_snake,
  input  [2:0] line_mushroom,
  input  [7:0] pos_snake,
  input  [7:0] pos_mushroom,
  output condition
);

  wire and_2_out, or_1_out;
  wire [2:0] xnor_1_out;
  wire [7:0] and_1_out;

  assign xnor_1_out = ~(line_snake ^ line_mushroom);  // XNOR_Gate xnor_1, 3 bits wide
  assign and_1_out = pos_snake & pos_mushroom;  // AND_Gate and_1, 8 bits wide
  and and_2 (and_2_out, xnor_1_out[0], xnor_1_out[1], xnor_1_out[2]);
  or or_1 (or_1_out, and_1_out[0], and_1_out[1], and_1_out[2], and_1_out[3], and_1_out[5], and_1_out[6], and_1_out[7], and_1_out[4]);
  and and_3 (condition, and_2_out, or_1_out);
endmodule

module next_mushroom (
  input  [2:0] positionline,
  input  [7:0] currentline,
  input  [7:0] in_3,
  input  [7:0] line_pos1,
  input  [7:0] line_pos2,
  input  [7:0] line_pos3,
  input  [7:0] linepos4,
  input  [7:0] linepos5,
  input  [7:0] linepos6,
  input  [7:0] linepos7,
  input  [7:0] linepos8,
  output condition_snake_is_on_mushrrom,
  output [7:0] pos
);

  wire condition_snakeisonmushroom_1_condition, condition_snakeisonmushroom_2_condition,
       condition_snakeisonmushroom_3_condition, condition_snakeisonmushroom_4_condition,
       condition_snakeisonmushroom_5_condition, condition_snakeisonmushroom_6_condition,
       condition_snakeisonmushroom_7_condition, condition_snakeisonmushroom_8_condition;

  condition_snakeisonmushroom condition_snakeisonmushroom_1 (
    .line_snake(positionline), .line_mushroom(3'b110), .pos_snake(currentline), .pos_mushroom(line_pos1),
    .condition(condition_snakeisonmushroom_1_condition));
  condition_snakeisonmushroom condition_snakeisonmushroom_2 (
    .line_snake(positionline), .line_mushroom(3'b010), .pos_snake(currentline), .pos_mushroom(line_pos2),
    .condition(condition_snakeisonmushroom_2_condition));
  condition_snakeisonmushroom condition_snakeisonmushroom_3 (
    .line_snake(positionline), .line_mushroom(3'b111), .pos_snake(currentline), .pos_mushroom(line_pos3),
    .condition(condition_snakeisonmushroom_3_condition));
  condition_snakeisonmushroom condition_snakeisonmushroom_4 (
    .line_snake(positionline), .line_mushroom(3'b011), .pos_snake(currentline), .pos_mushroom(linepos4),
    .condition(condition_snakeisonmushroom_4_condition));
  condition_snakeisonmushroom condition_snakeisonmushroom_5 (
    .line_snake(positionline), .line_mushroom(3'b101), .pos_snake(currentline), .pos_mushroom(linepos5),
    .condition(condition_snakeisonmushroom_5_condition));
  condition_snakeisonmushroom condition_snakeisonmushroom_6 (
    .line_snake(positionline), .line_mushroom(3'b000), .pos_snake(currentline), .pos_mushroom(linepos6),
    .condition(condition_snakeisonmushroom_6_condition));
  condition_snakeisonmushroom condition_snakeisonmushroom_7 (
    .line_snake(positionline), .line_mushroom(3'b001), .pos_snake(currentline), .pos_mushroom(linepos7),
    .condition(condition_snakeisonmushroom_7_condition));
  condition_snakeisonmushroom condition_snakeisonmushroom_8 (
    .line_snake(positionline), .line_mushroom(3'b100), .pos_snake(currentline), .pos_mushroom(linepos8),
    .condition(condition_snakeisonmushroom_8_condition));
  and and_1 (pos[6], in_3[7], condition_snakeisonmushroom_1_condition);
  and and_2 (pos[5], in_3[6], condition_snakeisonmushroom_2_condition);
  and and_3 (pos[4], in_3[5], condition_snakeisonmushroom_3_condition);
  and and_4 (pos[3], in_3[4], condition_snakeisonmushroom_4_condition);
  and and_5 (pos[2], in_3[3], condition_snakeisonmushroom_5_condition);
  and and_6 (pos[1], in_3[2], condition_snakeisonmushroom_6_condition);
  and and_7 (pos[0], in_3[1], condition_snakeisonmushroom_7_condition);
  and and_8 (pos[7], in_3[0], condition_snakeisonmushroom_8_condition);
  or or_1 (condition_snake_is_on_mushrrom, pos[0], pos[1], pos[2], pos[3], pos[5], pos[6], pos[7], pos[4]);
endmodule

module memorize_pos (
  input  reset,
  input  [7:0] pos,
  output [7:0] out_3
);

  wire or_1_out, or_2_out, or_3_out, or_4_out, or_5_out, or_6_out, or_7_out, or_8_out, or_9_out, or_10_out,
       or_11_out, or_12_out, or_13_out, or_14_out, or_15_out, or_16_out;

  or or_1 (or_1_out, pos[7], reset);
  or or_2 (or_2_out, pos[1], pos[2], pos[3], pos[4], pos[5], pos[6], or_1_out);
  SR sr_1 (.R(or_5_out), .S(pos[1]), .Q(out_3[1]));
  SR sr_2 (.R(or_7_out), .S(pos[2]), .Q(out_3[2]));
  SR sr_3 (.R(or_10_out), .S(pos[3]), .Q(out_3[3]));
  SR sr_4 (.R(or_12_out), .S(pos[4]), .Q(out_3[4]));
  SR sr_5 (.R(or_14_out), .S(pos[5]), .Q(out_3[5]));
  SR sr_6 (.R(or_16_out), .S(pos[6]), .Q(out_3[6]));
  SR sr_7 (.R(or_15_out), .S(or_1_out), .Q(out_3[7]));
  or or_3 (or_3_out, pos[0], pos[2], pos[3], pos[4], pos[5], pos[6], or_1_out);
  SR sr_8 (.R(or_4_out), .S(pos[0]), .Q(out_3[0]));
  or or_4 (or_4_out, reset, or_2_out);
  or or_5 (or_5_out, or_3_out, reset);
  or or_6 (or_6_out, pos[0], pos[1], pos[3], pos[4], pos[5], pos[6], or_1_out);
  or or_7 (or_7_out, reset, or_6_out);
  or or_8 (or_8_out, pos[0], pos[1], pos[2], pos[4], pos[5], pos[6], or_1_out);
  or or_9 (or_9_out, pos[0], pos[1], pos[2], pos[3], pos[5], pos[6], or_1_out);
  or or_10 (or_10_out, reset, or_8_out);
  or or_11 (or_11_out, pos[0], pos[1], pos[2], pos[3], pos[4], pos[6], or_1_out);
  or or_12 (or_12_out, reset, or_9_out);
  or or_13 (or_13_out, pos[0], pos[1], pos[2], pos[3], pos[4], pos[5], or_1_out);
  or or_14 (or_14_out, reset, or_11_out);
  or or_15 (or_15_out, pos[0], pos[1], pos[2], pos[3], pos[4], pos[5], pos[6]);
  or or_16 (or_16_out, reset, or_13_out);
endmodule

module general_body_snake (
  input  [7:0] current_line_snake,
  input  [2:0] position_line_snake,
  input  condition_mushroomonsnake,
  input  reset,
  input  clock,
  output [7:0] out_6,
  output [7:0] out_7,
  output [7:0] out_8,
  output [7:0] out_9,
  output [7:0] out_10,
  output [7:0] out_11,
  output [7:0] out_12,
  output [7:0] out_13,
  output L1,
  output L2,
  output L3,
  output L4,
  output L5,
  output L6,
  output L7
);

  wire memory_body_snake_1_condtion_memory, memory_body_snake_2_condtion_memory,
       memory_body_snake_3_condtion_memory, memory_body_snake_4_condtion_memory,
       memory_body_snake_5_condtion_memory, memory_body_snake_6_condtion_memory,
       memory_body_snake_7_condtion_memory;
  wire [2:0] memory_body_snake_1_position_line_2, memory_body_snake_2_position_line_2,
       memory_body_snake_3_position_line_2, memory_body_snake_4_position_line_2,
       memory_body_snake_5_position_line_2, memory_body_snake_6_position_line_2,
       memory_body_snake_7_position_line_2;
  wire [7:0] graphiq_link_1_a, graphiq_link_1_b, graphiq_link_1_c, graphiq_link_1_d, graphiq_link_1_e,
       graphiq_link_1_f, graphiq_link_1_g, graphiq_link_1_h, graphiq_link_2_a, graphiq_link_2_b,
       graphiq_link_2_c, graphiq_link_2_d, graphiq_link_2_e, graphiq_link_2_f, graphiq_link_2_g,
       graphiq_link_2_h, graphiq_link_3_a, graphiq_link_3_b, graphiq_link_3_c, graphiq_link_3_d,
       graphiq_link_3_e, graphiq_link_3_f, graphiq_link_3_g, graphiq_link_3_h, graphiq_link_4_a,
       graphiq_link_4_b, graphiq_link_4_c, graphiq_link_4_d, graphiq_link_4_e, graphiq_link_4_f,
       graphiq_link_4_g, graphiq_link_4_h, graphiq_link_5_a, graphiq_link_5_b, graphiq_link_5_c,
       graphiq_link_5_d, graphiq_link_5_e, graphiq_link_5_f, graphiq_link_5_g, graphiq_link_5_h,
       graphiq_link_6_a, graphiq_link_6_b, graphiq_link_6_c, graphiq_link_6_d, graphiq_link_6_e,
       graphiq_link_6_f, graphiq_link_6_g, graphiq_link_6_h, graphiq_link_7_a, graphiq_link_7_b,
       graphiq_link_7_c, graphiq_link_7_d, graphiq_link_7_e, graphiq_link_7_f, graphiq_link_7_g,
       graphiq_link_7_h, memory_body_snake_1_body_position, memory_body_snake_2_body_position,
       memory_body_snake_3_body_position, memory_body_snake_4_body_position,
       memory_body_snake_5_body_position, memory_body_snake_6_body_position,
       memory_body_snake_7_body_position;

  memory_body_snake memory_body_snake_1 (
    .condition_mushroomsnake(condition_mushroomonsnake), .condition_memory(1'b1),
    .current_line(current_line_snake), .position_line(position_line_snake), .reset(reset), .clock(clock),
    .body_position(memory_body_snake_1_body_position), .position_line_2(memory_body_snake_1_position_line_2),
    .condtion_memory(memory_body_snake_1_condtion_memory));
  memory_body_snake memory_body_snake_2 (
    .condition_mushroomsnake(condition_mushroomonsnake),
    .condition_memory(memory_body_snake_1_condtion_memory), .current_line(memory_body_snake_1_body_position),
    .position_line(memory_body_snake_1_position_line_2), .reset(reset), .clock(clock),
    .body_position(memory_body_snake_2_body_position), .position_line_2(memory_body_snake_2_position_line_2),
    .condtion_memory(memory_body_snake_2_condtion_memory));
  memory_body_snake memory_body_snake_3 (
    .condition_mushroomsnake(condition_mushroomonsnake),
    .condition_memory(memory_body_snake_2_condtion_memory), .current_line(memory_body_snake_2_body_position),
    .position_line(memory_body_snake_2_position_line_2), .reset(reset), .clock(clock),
    .body_position(memory_body_snake_3_body_position), .position_line_2(memory_body_snake_3_position_line_2),
    .condtion_memory(memory_body_snake_3_condtion_memory));
  memory_body_snake memory_body_snake_4 (
    .condition_mushroomsnake(condition_mushroomonsnake),
    .condition_memory(memory_body_snake_3_condtion_memory), .current_line(memory_body_snake_3_body_position),
    .position_line(memory_body_snake_3_position_line_2), .reset(reset), .clock(clock),
    .body_position(memory_body_snake_4_body_position), .position_line_2(memory_body_snake_4_position_line_2),
    .condtion_memory(memory_body_snake_4_condtion_memory));
  memory_body_snake memory_body_snake_5 (
    .condition_mushroomsnake(condition_mushroomonsnake),
    .condition_memory(memory_body_snake_4_condtion_memory), .current_line(memory_body_snake_4_body_position),
    .position_line(memory_body_snake_4_position_line_2), .reset(reset), .clock(clock),
    .body_position(memory_body_snake_5_body_position), .position_line_2(memory_body_snake_5_position_line_2),
    .condtion_memory(memory_body_snake_5_condtion_memory));
  memory_body_snake memory_body_snake_6 (
    .condition_mushroomsnake(condition_mushroomonsnake),
    .condition_memory(memory_body_snake_5_condtion_memory), .current_line(memory_body_snake_5_body_position),
    .position_line(memory_body_snake_5_position_line_2), .reset(reset), .clock(clock),
    .body_position(memory_body_snake_6_body_position), .position_line_2(memory_body_snake_6_position_line_2),
    .condtion_memory(memory_body_snake_6_condtion_memory));
  memory_body_snake memory_body_snake_7 (
    .condition_mushroomsnake(condition_mushroomonsnake),
    .condition_memory(memory_body_snake_6_condtion_memory), .current_line(memory_body_snake_6_body_position),
    .position_line(memory_body_snake_6_position_line_2), .reset(reset), .clock(clock),
    .body_position(memory_body_snake_7_body_position), .position_line_2(memory_body_snake_7_position_line_2),
    .condtion_memory(memory_body_snake_7_condtion_memory));
  graphiq_link graphiq_link_1 (
    .position(memory_body_snake_1_position_line_2), .line(memory_body_snake_1_body_position),
    .a(graphiq_link_1_a), .b(graphiq_link_1_b), .c(graphiq_link_1_c), .d(graphiq_link_1_d),
    .e(graphiq_link_1_e), .f(graphiq_link_1_f), .g(graphiq_link_1_g), .h(graphiq_link_1_h));
  graphiq_link graphiq_link_2 (
    .position(memory_body_snake_2_position_line_2), .line(memory_body_snake_2_body_position),
    .a(graphiq_link_2_a), .b(graphiq_link_2_b), .c(graphiq_link_2_c), .d(graphiq_link_2_d),
    .e(graphiq_link_2_e), .f(graphiq_link_2_f), .g(graphiq_link_2_g), .h(graphiq_link_2_h));
  graphiq_link graphiq_link_3 (
    .position(memory_body_snake_3_position_line_2), .line(memory_body_snake_3_body_position),
    .a(graphiq_link_3_a), .b(graphiq_link_3_b), .c(graphiq_link_3_c), .d(graphiq_link_3_d),
    .e(graphiq_link_3_e), .f(graphiq_link_3_f), .g(graphiq_link_3_g), .h(graphiq_link_3_h));
  graphiq_link graphiq_link_4 (
    .position(memory_body_snake_4_position_line_2), .line(memory_body_snake_4_body_position),
    .a(graphiq_link_4_a), .b(graphiq_link_4_b), .c(graphiq_link_4_c), .d(graphiq_link_4_d),
    .e(graphiq_link_4_e), .f(graphiq_link_4_f), .g(graphiq_link_4_g), .h(graphiq_link_4_h));
  graphiq_link graphiq_link_5 (
    .position(memory_body_snake_5_position_line_2), .line(memory_body_snake_5_body_position),
    .a(graphiq_link_5_a), .b(graphiq_link_5_b), .c(graphiq_link_5_c), .d(graphiq_link_5_d),
    .e(graphiq_link_5_e), .f(graphiq_link_5_f), .g(graphiq_link_5_g), .h(graphiq_link_5_h));
  graphiq_link graphiq_link_6 (
    .position(memory_body_snake_6_position_line_2), .line(memory_body_snake_6_body_position),
    .a(graphiq_link_6_a), .b(graphiq_link_6_b), .c(graphiq_link_6_c), .d(graphiq_link_6_d),
    .e(graphiq_link_6_e), .f(graphiq_link_6_f), .g(graphiq_link_6_g), .h(graphiq_link_6_h));
  graphiq_link graphiq_link_7 (
    .position(memory_body_snake_7_position_line_2), .line(memory_body_snake_7_body_position),
    .a(graphiq_link_7_a), .b(graphiq_link_7_b), .c(graphiq_link_7_c), .d(graphiq_link_7_d),
    .e(graphiq_link_7_e), .f(graphiq_link_7_f), .g(graphiq_link_7_g), .h(graphiq_link_7_h));
  assign out_6 = graphiq_link_1_a | graphiq_link_2_a | graphiq_link_3_a | graphiq_link_4_a | graphiq_link_5_a | graphiq_link_6_a | graphiq_link_7_a;  // OR_Gate or_1, 8 bits wide
  assign out_7 = graphiq_link_1_b | graphiq_link_2_b | graphiq_link_3_b | graphiq_link_4_b | graphiq_link_5_b | graphiq_link_6_b | graphiq_link_7_b;  // OR_Gate or_2, 8 bits wide
  assign out_8 = graphiq_link_1_c | graphiq_link_2_c | graphiq_link_3_c | graphiq_link_4_c | graphiq_link_5_c | graphiq_link_6_c | graphiq_link_7_c;  // OR_Gate or_3, 8 bits wide
  assign out_9 = graphiq_link_1_d | graphiq_link_2_d | graphiq_link_3_d | graphiq_link_4_d | graphiq_link_5_d | graphiq_link_6_d | graphiq_link_7_d;  // OR_Gate or_4, 8 bits wide
  assign out_10 = graphiq_link_1_e | graphiq_link_2_e | graphiq_link_3_e | graphiq_link_4_e | graphiq_link_5_e | graphiq_link_6_e | graphiq_link_7_e;  // OR_Gate or_5, 8 bits wide
  assign out_11 = graphiq_link_1_f | graphiq_link_2_f | graphiq_link_3_f | graphiq_link_4_f | graphiq_link_5_f | graphiq_link_6_f | graphiq_link_7_f;  // OR_Gate or_6, 8 bits wide
  assign out_12 = graphiq_link_1_g | graphiq_link_2_g | graphiq_link_3_g | graphiq_link_4_g | graphiq_link_5_g | graphiq_link_6_g | graphiq_link_7_g;  // OR_Gate or_7, 8 bits wide
  assign out_13 = graphiq_link_1_h | graphiq_link_2_h | graphiq_link_3_h | graphiq_link_4_h | graphiq_link_5_h | graphiq_link_6_h | graphiq_link_7_h;  // OR_Gate or_8, 8 bits wide
  Affichage_score affichage_score_1 (
    .reset(reset), .cond7(memory_body_snake_7_condtion_memory), .cond6(memory_body_snake_6_condtion_memory),
    .cond5(memory_body_snake_5_condtion_memory), .cond4(memory_body_snake_4_condtion_memory),
    .cond3(memory_body_snake_3_condtion_memory), .cond2(memory_body_snake_2_condtion_memory),
    .cond1(memory_body_snake_1_condtion_memory), .cond0(1'b1), .L1(L1), .L2(L2), .L3(L3), .L4(L4), .L5(L5),
    .L6(L6), .L7(L7));
endmodule

module memory_body_snake (
  input  condition_mushroomsnake,
  input  condition_memory,
  input  [7:0] current_line,
  input  [2:0] position_line,
  input  reset,
  input  clock,
  output [7:0] body_position,
  output [2:0] position_line_2,
  output condtion_memory
);

  wire and_1_out, not_1_out, or_1_out;
  wire [2:0] and_3_out;
  wire [2:2] not_2_out, sr_1_q;
  wire [7:0] and_2_out;

  or or_1 (or_1_out, not_1_out, reset);
  not not_1 (not_1_out, condition_memory);
  SR sr_1 (.R(or_1_out), .S(condition_mushroomsnake), .Q(sr_1_q[2]));
  not not_2 (not_2_out[2], reset);
  and and_1 (and_1_out, condition_memory, sr_1_q[2]);
  D_Flip_Flop d_ff_1 (.D(and_1_out), .clk(clock), .Q(condtion_memory));  // open: Qn, preset, reset
  assign and_2_out = {8{sr_1_q[2]}} & {8{condition_memory}} & current_line & {8{not_2_out[2]}};  // AND_Gate and_2, 8 bits wide
  assign and_3_out = {3{sr_1_q[2]}} & {3{condition_memory}} & position_line & {3{not_2_out[2]}};  // AND_Gate and_3, 3 bits wide
  D_Flip_Flop d_ff_2 (.D(and_3_out[0]), .clk(clock), .Q(position_line_2[0]), .reset(reset));  // open: Qn, preset
  D_Flip_Flop d_ff_3 (.D(and_2_out[0]), .clk(clock), .Q(body_position[0]), .reset(reset));  // open: Qn, preset
  D_Flip_Flop d_ff_4 (.D(and_2_out[2]), .clk(clock), .Q(body_position[2]), .reset(reset));  // open: Qn, preset
  D_Flip_Flop d_ff_5 (.D(and_2_out[4]), .clk(clock), .Q(body_position[4]), .reset(reset));  // open: Qn, preset
  D_Flip_Flop d_ff_6 (.D(and_2_out[6]), .clk(clock), .Q(body_position[6]), .reset(reset));  // open: Qn, preset
  D_Flip_Flop d_ff_7 (.D(and_3_out[1]), .clk(clock), .Q(position_line_2[1]), .reset(reset));  // open: Qn, preset
  D_Flip_Flop d_ff_8 (.D(and_2_out[1]), .clk(clock), .Q(body_position[1]), .reset(reset));  // open: Qn, preset
  D_Flip_Flop d_ff_9 (.D(and_2_out[3]), .clk(clock), .Q(body_position[3]), .reset(reset));  // open: Qn, preset
  D_Flip_Flop d_ff_10 (.D(and_2_out[5]), .clk(clock), .Q(body_position[5]), .reset(reset));  // open: Qn, preset
  D_Flip_Flop d_ff_11 (.D(and_2_out[7]), .clk(clock), .Q(body_position[7]), .reset(reset));  // open: Qn, preset
  D_Flip_Flop d_ff_12 (.D(and_3_out[2]), .clk(clock), .Q(position_line_2[2]), .reset(reset));  // open: Qn, preset
endmodule

// General
module general_mothafucka (
  input  g,
  input  d,
  input  h,
  input  b,
  input  reset,
  input  clock,
  output [7:0] out_7,
  output [7:0] out_8,
  output [7:0] out_9,
  output [7:0] out_10,
  output [7:0] out_11,
  output [7:0] out_12,
  output [7:0] out_13,
  output [7:0] out_14,
  output reset_2,
  output [6:0] out_16
);

  wire general_mushroom_and_snake_1_conditon1, snakebitsnakeyeah_1_resetyeahbit;
  wire [2:0] general_mushroom_and_snake_1_position_line;
  wire [7:0] general_body_snake_1_out_6, general_body_snake_1_out_7, general_body_snake_1_out_8,
       general_body_snake_1_out_9, general_body_snake_1_out_10, general_body_snake_1_out_11,
       general_body_snake_1_out_12, general_body_snake_1_out_13, general_mushroom_and_snake_1_current_line,
       general_mushroom_and_snake_1_ms1, general_mushroom_and_snake_1_out_16,
       general_mushroom_and_snake_1_out_17, general_mushroom_and_snake_1_out_18,
       general_mushroom_and_snake_1_out_19, general_mushroom_and_snake_1_out_20,
       general_mushroom_and_snake_1_out_21, general_mushroom_and_snake_1_out_22,
       general_mushroom_and_snake_1_s1, general_mushroom_and_snake_1_s2, general_mushroom_and_snake_1_s3,
       general_mushroom_and_snake_1_s4, general_mushroom_and_snake_1_s5, general_mushroom_and_snake_1_s6,
       general_mushroom_and_snake_1_s7, general_mushroom_and_snake_1_s8;

  general_mushroom_and_snake general_mushroom_and_snake_1 (
    .g(g), .d(d), .h(h), .b(b), .reset(reset), .clock(clock), .s1(general_mushroom_and_snake_1_s1),
    .s2(general_mushroom_and_snake_1_s2), .s3(general_mushroom_and_snake_1_s3),
    .s4(general_mushroom_and_snake_1_s4), .s5(general_mushroom_and_snake_1_s5),
    .s6(general_mushroom_and_snake_1_s6), .s7(general_mushroom_and_snake_1_s7),
    .s8(general_mushroom_and_snake_1_s8), .ms1(general_mushroom_and_snake_1_ms1),
    .out_16(general_mushroom_and_snake_1_out_16), .out_17(general_mushroom_and_snake_1_out_17),
    .out_18(general_mushroom_and_snake_1_out_18), .out_19(general_mushroom_and_snake_1_out_19),
    .out_20(general_mushroom_and_snake_1_out_20), .out_21(general_mushroom_and_snake_1_out_21),
    .out_22(general_mushroom_and_snake_1_out_22), .position_line(general_mushroom_and_snake_1_position_line),
    .current_line(general_mushroom_and_snake_1_current_line),
    .conditon1(general_mushroom_and_snake_1_conditon1), .reset_2(reset_2));
  general_body_snake general_body_snake_1 (
    .current_line_snake(general_mushroom_and_snake_1_current_line),
    .position_line_snake(general_mushroom_and_snake_1_position_line),
    .condition_mushroomonsnake(general_mushroom_and_snake_1_conditon1), .reset(reset), .clock(clock),
    .out_6(general_body_snake_1_out_6), .out_7(general_body_snake_1_out_7),
    .out_8(general_body_snake_1_out_8), .out_9(general_body_snake_1_out_9),
    .out_10(general_body_snake_1_out_10), .out_11(general_body_snake_1_out_11),
    .out_12(general_body_snake_1_out_12), .out_13(general_body_snake_1_out_13), .L1(out_16[0]),
    .L2(out_16[1]), .L3(out_16[2]), .L4(out_16[3]), .L5(out_16[4]), .L6(out_16[5]), .L7(out_16[6]));
  assign out_7 = general_mushroom_and_snake_1_ms1 | general_body_snake_1_out_6;  // OR_Gate or_1, 8 bits wide
  assign out_8 = general_mushroom_and_snake_1_out_16 | general_body_snake_1_out_7;  // OR_Gate or_2, 8 bits wide
  assign out_9 = general_mushroom_and_snake_1_out_17 | general_body_snake_1_out_8;  // OR_Gate or_3, 8 bits wide
  assign out_10 = general_mushroom_and_snake_1_out_18 | general_body_snake_1_out_9;  // OR_Gate or_4, 8 bits wide
  assign out_11 = general_mushroom_and_snake_1_out_19 | general_body_snake_1_out_10;  // OR_Gate or_5, 8 bits wide
  assign out_12 = general_mushroom_and_snake_1_out_20 | general_body_snake_1_out_11;  // OR_Gate or_6, 8 bits wide
  assign out_13 = general_mushroom_and_snake_1_out_21 | general_body_snake_1_out_12;  // OR_Gate or_7, 8 bits wide
  assign out_14 = general_mushroom_and_snake_1_out_22 | general_body_snake_1_out_13;  // OR_Gate or_8, 8 bits wide
  snakebitsnakeyeah snakebitsnakeyeah_1 (
    .head1(general_mushroom_and_snake_1_s1), .head2(general_mushroom_and_snake_1_s2),
    .head3(general_mushroom_and_snake_1_s3), .head4(general_mushroom_and_snake_1_s4),
    .head5(general_mushroom_and_snake_1_s5), .head6(general_mushroom_and_snake_1_s6),
    .head7(general_mushroom_and_snake_1_s7), .head8(general_mushroom_and_snake_1_s8),
    .body1(general_body_snake_1_out_6), .bod2(general_body_snake_1_out_7),
    .body3(general_body_snake_1_out_8), .body4(general_body_snake_1_out_9),
    .body5(general_body_snake_1_out_10), .body6(general_body_snake_1_out_11),
    .body7(general_body_snake_1_out_12), .body8(general_body_snake_1_out_13),
    .resetyeahbit(snakebitsnakeyeah_1_resetyeahbit));
endmodule

module snakebitsnakeyeah (
  input  [7:0] head1,
  input  [7:0] head2,
  input  [7:0] head3,
  input  [7:0] head4,
  input  [7:0] head5,
  input  [7:0] head6,
  input  [7:0] head7,
  input  [7:0] head8,
  input  [7:0] body1,
  input  [7:0] bod2,
  input  [7:0] body3,
  input  [7:0] body4,
  input  [7:0] body5,
  input  [7:0] body6,
  input  [7:0] body7,
  input  [7:0] body8,
  output resetyeahbit
);

  wire [7:0] and_1_out, and_2_out, and_3_out, and_4_out, and_5_out, and_6_out, and_7_out, and_8_out, or_1_out;

  assign and_1_out = head1 & body1;  // AND_Gate and_1, 8 bits wide
  assign and_2_out = head2 & bod2;  // AND_Gate and_2, 8 bits wide
  assign and_3_out = head3 & body3;  // AND_Gate and_3, 8 bits wide
  assign and_4_out = head4 & body4;  // AND_Gate and_4, 8 bits wide
  assign and_5_out = head5 & body5;  // AND_Gate and_5, 8 bits wide
  assign and_6_out = head6 & body6;  // AND_Gate and_6, 8 bits wide
  assign and_7_out = head7 & body7;  // AND_Gate and_7, 8 bits wide
  assign and_8_out = head8 & body8;  // AND_Gate and_8, 8 bits wide
  assign or_1_out = and_1_out | and_2_out | and_3_out | and_4_out | and_5_out | and_6_out | and_7_out | and_8_out;  // OR_Gate or_1, 8 bits wide
  or or_2 (resetyeahbit, or_1_out[0], or_1_out[1], or_1_out[2], or_1_out[3], or_1_out[5], or_1_out[6], or_1_out[7], or_1_out[4]);
endmodule

module Affichage_score (
  input  reset,
  input  cond7,
  input  cond6,
  input  cond5,
  input  cond4,
  input  cond3,
  input  cond2,
  input  cond1,
  input  cond0,
  output L1,
  output L2,
  output L3,
  output L4,
  output L5,
  output L6,
  output L7
);

  wire and_1_out, and_2_out, and_3_out, and_4_out, and_5_out, and_6_out, and_7_out, and_8_out, and_9_out,
       and_10_out, and_11_out, and_12_out, and_13_out, and_14_out, and_15_out, and_16_out, and_17_out,
       and_18_out, and_19_out, and_20_out, and_21_out, and_22_out, and_23_out, and_24_out, and_25_out,
       and_26_out, and_27_out, and_28_out, and_29_out, and_30_out, not_1_out, not_2_out, not_3_out,
       not_4_out, not_5_out, not_6_out, not_7_out, not_8_out, not_9_out, not_10_out, not_11_out, not_12_out,
       not_13_out, not_14_out, not_15_out, not_16_out, not_17_out, not_18_out, not_19_out, not_20_out,
       not_21_out, not_22_out, not_23_out, not_24_out, not_25_out, not_26_out, not_27_out, not_28_out,
       not_29_out, not_30_out, not_31_out, not_32_out, not_33_out, not_34_out, not_35_out, not_36_out,
       not_37_out, not_38_out, not_39_out, not_40_out, not_41_out, not_42_out, not_43_out, not_44_out,
       not_45_out, not_46_out, not_47_out, not_48_out, not_49_out, not_50_out, not_51_out, not_52_out,
       not_53_out, not_54_out, not_55_out, not_56_out, not_57_out, not_58_out, not_59_out, not_60_out,
       not_61_out, not_62_out, not_63_out, not_64_out, not_65_out, not_66_out, not_67_out, not_68_out;

  not not_1 (not_1_out, cond6);
  not not_2 (not_2_out, cond5);
  not not_3 (not_3_out, cond7);
  not not_4 (not_4_out, cond5);
  not not_5 (not_5_out, cond4);
  not not_6 (not_6_out, cond3);
  not not_7 (not_7_out, cond2);
  not not_8 (not_8_out, cond1);
  not not_9 (not_9_out, cond6);
  not not_10 (not_10_out, cond2);
  not not_11 (not_11_out, cond7);
  not not_12 (not_12_out, cond6);
  not not_13 (not_13_out, cond5);
  not not_14 (not_14_out, cond7);
  not not_15 (not_15_out, cond6);
  not not_16 (not_16_out, cond7);
  not not_17 (not_17_out, cond4);
  not not_18 (not_18_out, cond1);
  not not_19 (not_19_out, cond7);
  not not_20 (not_20_out, cond6);
  not not_21 (not_21_out, cond5);
  not not_22 (not_22_out, cond4);
  not not_23 (not_23_out, cond7);
  not not_24 (not_24_out, cond7);
  not not_25 (not_25_out, cond5);
  not not_26 (not_26_out, cond4);
  not not_27 (not_27_out, cond3);
  not not_28 (not_28_out, cond1);
  not not_29 (not_29_out, cond7);
  not not_30 (not_30_out, cond6);
  not not_31 (not_31_out, cond5);
  not not_32 (not_32_out, cond4);
  not not_33 (not_33_out, cond3);
  not not_34 (not_34_out, cond7);
  not not_35 (not_35_out, reset);
  not not_36 (not_36_out, cond3);
  not not_37 (not_37_out, reset);
  not not_38 (not_38_out, cond7);
  not not_39 (not_39_out, reset);
  not not_40 (not_40_out, cond7);
  not not_41 (not_41_out, reset);
  not not_42 (not_42_out, cond7);
  not not_43 (not_43_out, reset);
  not not_44 (not_44_out, cond5);
  not not_45 (not_45_out, reset);
  not not_46 (not_46_out, cond4);
  not not_47 (not_47_out, reset);
  not not_48 (not_48_out, cond0);
  not not_49 (not_49_out, reset);
  not not_50 (not_50_out, cond6);
  not not_51 (not_51_out, reset);
  not not_52 (not_52_out, cond2);
  not not_53 (not_53_out, reset);
  not not_54 (not_54_out, cond1);
  not not_55 (not_55_out, cond7);
  not not_56 (not_56_out, cond3);
  not not_57 (not_57_out, cond2);
  not not_58 (not_58_out, cond1);
  not not_59 (not_59_out, cond7);
  not not_60 (not_60_out, cond6);
  not not_61 (not_61_out, cond7);
  not not_62 (not_62_out, cond4);
  not not_63 (not_63_out, cond1);
  not not_64 (not_64_out, cond7);
  not not_65 (not_65_out, cond6);
  not not_66 (not_66_out, cond5);
  not not_67 (not_67_out, cond4);
  not not_68 (not_68_out, cond7);
  and and_1 (and_1_out, not_1_out, not_2_out);
  and and_2 (and_2_out, not_3_out, not_4_out, not_5_out, not_6_out, not_7_out, not_8_out, cond0);
  and and_3 (and_3_out, cond7, cond6, cond5, cond4, cond3, cond2, cond1, cond0);
  and and_4 (and_4_out, not_9_out, not_10_out);
  and and_5 (and_5_out, not_11_out, not_12_out, not_13_out, cond3, cond1, cond0);
  and and_6 (and_6_out, not_14_out, not_15_out, cond4, cond3, cond1, cond0);
  and and_7 (and_7_out, cond6, cond5, cond4, cond3, cond2, cond1, cond0);
  and and_8 (and_8_out, not_16_out, not_17_out, not_18_out);
  and and_9 (and_9_out, not_19_out, not_20_out, not_21_out, not_22_out, cond2, cond0);
  and and_10 (and_10_out, not_23_out, cond5, cond4, cond3, cond2, cond1, cond0);
  and and_11 (and_11_out, not_24_out, not_25_out, not_26_out, not_27_out, not_28_out);
  and and_12 (and_12_out, not_29_out, not_30_out, not_31_out, not_32_out, not_33_out, cond2, cond0);
  and and_13 (and_13_out, not_34_out, cond6, cond5, cond4, cond3, cond2, cond1, cond0);
  and and_14 (and_14_out, not_35_out, not_36_out, cond2);
  and and_15 (and_15_out, not_37_out, not_38_out, cond3);
  and and_16 (and_16_out, not_39_out, not_40_out, cond4);
  and and_17 (and_17_out, not_41_out, not_42_out, cond5);
  and and_18 (and_18_out, not_43_out, cond6, not_44_out);
  and and_19 (and_19_out, not_45_out, cond6, not_46_out);
  and and_20 (and_20_out, not_47_out, cond6, not_48_out);
  and and_21 (and_21_out, not_49_out, cond7, not_50_out);
  and and_22 (and_22_out, not_51_out, cond7, not_52_out);
  and and_23 (and_23_out, not_53_out, cond7, not_54_out);
  and and_24 (and_24_out, not_55_out, not_56_out, not_57_out, not_58_out);
  and and_25 (and_25_out, not_59_out, not_60_out, cond4, cond3, cond2, cond1, cond0);
  and and_26 (and_26_out, not_61_out, cond5, cond4, cond3, cond2, cond1, cond0);
  and and_27 (and_27_out, not_62_out, not_63_out);
  and and_28 (and_28_out, not_64_out, not_65_out, not_66_out, not_67_out, cond2, cond0);
  and and_29 (and_29_out, not_68_out, cond5, cond4, cond3, cond2, cond1, cond0);
  and and_30 (and_30_out, cond6, cond5, cond4, cond3, cond2, cond1, cond0);
  or or_1 (L1, and_1_out, and_2_out, and_3_out, reset);
  or or_2 (L2, and_4_out, and_5_out, and_6_out, and_7_out, reset);
  or or_3 (L3, and_8_out, and_9_out, and_10_out, reset);
  or or_4 (L4, and_11_out, and_12_out, and_13_out, reset);
  or or_5 (L5, and_14_out, and_15_out, and_16_out, and_17_out, and_18_out, and_19_out, and_20_out, and_21_out, and_22_out, and_23_out);
  or or_6 (L6, and_24_out, and_25_out, and_26_out, reset);
  or or_7 (L7, and_27_out, and_28_out, and_29_out, and_30_out, reset);
endmodule
